# Fritzing sketch sketch (saved by Fritzing 0.9.2b)
breadboards: 1

parts:
  Part1 = Photon
  RHT1 = Humidity and Temperature Sensor RHT03
  R1 = Resistor [tolerance=±5% resistance=100 package=THT]

nets:
  N1: Part1.GND, RHT1.GND_2
  N2: Part1.D2, RHT1.Data-signal, R1.Pin_1
  3V3: Part1.3V3, RHT1.Vcc, R1.Pin_0

notes:
  rite your note here]
  ite your note here]
  note here]
  DHT 11 Sensor
